# Fritzing sketch Pushbutton (saved by Fritzing 0.9.4)
breadboards: 1

parts:
  Mod1 = Raspberry Pi 4B
  LED1 = smd LED [color="Red (633nm)" package="0805 [SMD]"]
  R1 = Resistor [tolerance=±5% resistance=220 package="0805 [SMD]"]
  S1 = Pushbutton [package="[THT]"]

nets:
  N1: Mod1.GPIO14, LED1.anode
  N2: Mod1.GND, S1.Pin_3, S1.Pin_4
  N3: Mod1.GPIO17, S1.Pin_1, S1.Pin_2
  N4: LED1.cathode, R1.Pin_0
