# Fritzing sketch blink (saved by Fritzing 0.9.4)
circuit board: 8.46667cm x 5.64444cm
breadboards: 1

parts:
  Mod1 = Raspberry Pi 4B
  LED1 = smd LED [color="Red (633nm)" package="0805 [SMD]"]
  R1 = Resistor [tolerance=±5% resistance=220 package="0805 [SMD]"]

nets:
  N1: Mod1.GND, R1.Pin_1
  N2: Mod1.GPIO14, LED1.anode
  N3: LED1.cathode, R1.Pin_0
